# Fritzing sketch schematic (saved by Fritzing 0.9.10b)

parts:
  Part1 = Arduino Nano (Rev3.0)
  ROM4 = 74HC595 [package="DIP16 [THT]"]
  ROM3 = 74HC595 [package="DIP16 [THT]"]
  CDATA_Bus = shrouded pin header, 8 pins [form="♂ (shrouded male)"]
  ROM2 = 74HC595 [package="DIP16 [THT]"]
  ROM1 = 74HC595 [package="DIP16 [THT]"]
  ALUOP_1 = female pin header, 1 pin [form="♀ (female)"]
  Z_SRC_C_DATA = female pin header, 1 pin [form="♀ (female)"]
  uJMP = female pin header, 1 pin [form="♀ (female)"]
  uJMPINV = female pin header, 1 pin [form="♀ (female)"]
  uP0 = female pin header, 1 pin [form="♀ (female)"]
  uP1 = female pin header, 1 pin [form="♀ (female)"]
  uP2 = female pin header, 1 pin [form="♀ (female)"]
  uZJMP = female pin header, 1 pin [form="♀ (female)"]
  A_OUT_CDATA = female pin header, 1 pin [form="♀ (female)"]
  ALUOP_0 = female pin header, 1 pin [form="♀ (female)"]
  ALUR_OUT_CDATA = female pin header, 1 pin [form="♀ (female)"]
  ALUB_LD_CDATA = female pin header, 1 pin [form="♀ (female)"]
  ALUA_LD_CDATA = female pin header, 1 pin [form="♀ (female)"]
  X_LD_CDATA = female pin header, 1 pin [form="♀ (female)"]
  X_OUT_CDATA = female pin header, 1 pin [form="♀ (female)"]
  PZ_LD = female pin header, 1 pin [form="♀ (female)"]
  PC_LD_CDATA = female pin header, 1 pin [form="♀ (female)"]
  A_LD_CDATA = female pin header, 1 pin [form="♀ (female)"]
  PC_OUT_CADDR = female pin header, 1 pin [form="♀ (female)"]
  MBR_OUT_CDATA = female pin header, 1 pin [form="♀ (female)"]
  PC_INC = female pin header, 1 pin [form="♀ (female)"]
  PC_REL_CDATA = female pin header, 1 pin [form="♀ (female)"]
  PC_OUT_CDATA = female pin header, 1 pin [form="♀ (female)"]
  MAR_LD_CDATA = female pin header, 1 pin [form="♀ (female)"]
  CDATA_LD_0 = female pin header, 1 pin [form="♀ (female)"]
  MBR_LD_XDATA = female pin header, 1 pin [form="♀ (female)"]
  CDATA_TO_CADDR = female pin header, 1 pin [form="♀ (female)"]
  MEM_OUT_XDATA = female pin header, 1 pin [form="♀ (female)"]
  IR_LD_XDATA = female pin header, 1 pin [form="♀ (female)"]
  MEM_LD_XDATA = female pin header, 1 pin [form="♀ (female)"]
  MBR_OUT_XDATA = female pin header, 1 pin [form="♀ (female)"]
  MBR_LD_CDATA = female pin header, 1 pin [form="♀ (female)"]
  CLOCK_OUT = female pin header, 1 pin [form="♀ (female)"]
  PZ_IN = female pin header, 1 pin [form="♀ (female)"]

nets:
  GND: Part1.GND, ROM4.GND, ROM4.OE, ROM3.GND, ROM3.OE, ROM2.GND, ROM2.OE, ROM1.GND, ROM1.OE
  N1: Part1.D2, ROM4.DS
  N2: Part1.D3, ROM4.SH_CP, ROM3.SH_CP, ROM2.SH_CP, ROM1.SH_CP
  N3: Part1.D4, ROM4.ST_CP, ROM3.ST_CP, ROM2.ST_CP, ROM1.ST_CP
  N4: Part1.D5, CDATA_Bus.pin1
  N5: Part1.D6, CDATA_Bus.pin2
  N6: Part1.D7, CDATA_Bus.pin3
  N7: Part1.D8, CDATA_Bus.pin4
  N8: Part1.D9, CDATA_Bus.pin5
  N9: Part1.D10, CDATA_Bus.pin6
  N10: Part1.D11/MOSI, CDATA_Bus.pin7
  N11: Part1.D12/MISO, CDATA_Bus.pin8
  N12: Part1.A0, PZ_IN.pin1
  5V: Part1.3V3, ROM4.MR, ROM4.VCC, ROM3.MR, ROM3.VCC, ROM2.MR, ROM2.VCC, ROM1.MR, ROM1.VCC
  N13: Part1.D13/SCK, CLOCK_OUT.pin1
  N14: ROM4.Q1, Z_SRC_C_DATA.pin1
  N15: ROM4.Q2, uJMP.pin1
  N16: ROM4.Q3, uJMPINV.pin1
  N17: ROM4.Q4, uP0.pin1
  N18: ROM4.Q5, uP1.pin1
  N19: ROM4.Q6, uP2.pin1
  N20: ROM4.Q7, uZJMP.pin1
  N21: ROM4.Q7', ROM3.DS
  N22: ROM4.Q0, ALUOP_1.pin1
  N23: ROM3.Q1, X_LD_CDATA.pin1
  N24: ROM3.Q2, X_OUT_CDATA.pin1
  N25: ROM3.Q3, PZ_LD.pin1
  N26: ROM3.Q4, ALUA_LD_CDATA.pin1
  N27: ROM3.Q5, ALUB_LD_CDATA.pin1
  N28: ROM3.Q6, ALUR_OUT_CDATA.pin1
  N29: ROM3.Q7, ALUOP_0.pin1
  N30: ROM3.Q7', ROM2.DS
  N31: ROM3.Q0, A_OUT_CDATA.pin1
  N32: ROM2.Q1, MAR_LD_CDATA.pin1
  N33: ROM2.Q2, PC_INC.pin1
  N34: ROM2.Q3, PC_REL_CDATA.pin1
  N35: ROM2.Q4, PC_LD_CDATA.pin1
  N36: ROM2.Q5, PC_OUT_CDATA.pin1
  N37: ROM2.Q6, PC_OUT_CADDR.pin1
  N38: ROM2.Q7, A_LD_CDATA.pin1
  N39: ROM2.Q7', ROM1.DS
  N40: ROM2.Q0, MBR_OUT_CDATA.pin1
  N41: ROM1.Q1, CDATA_TO_CADDR.pin1
  N42: ROM1.Q2, MEM_LD_XDATA.pin1
  N43: ROM1.Q3, MEM_OUT_XDATA.pin1
  N44: ROM1.Q4, IR_LD_XDATA.pin1
  N45: ROM1.Q5, MBR_LD_XDATA.pin1
  N46: ROM1.Q6, MBR_OUT_XDATA.pin1
  N47: ROM1.Q7, MBR_LD_CDATA.pin1
  N48: ROM1.Q0, CDATA_LD_0.pin1
